# Fritzing sketch Schematic (saved by Fritzing 0.9.3b)
breadboards: 1

parts:
  U1 = NodeMCU V1.0
  Module_Relay = female pin header, 6 pins [form="♀ (female)"]
  Buzzer = female pin header, 3 pins [form="♀ (female)"]
  Part1 = I2C level shifter bidirectional
  LCD = female pin header, 4 pins [form="♀ (female)"]
  Power_Sensor = female pin header, 4 pins [form="♀ (female)"]

nets:
  SCL ESP: U1.D1, Part1.LV4
  SDA ESP: U1.D2, Part1.LV3
  LOAD 1: U1.D3, Module_Relay.pin2
  LOAD 2: U1.D4, Module_Relay.pin3
  3.3V: U1.3V3, Buzzer.pin1, Part1.LV
  GND: U1.GND, Module_Relay.pin6, Buzzer.pin3, Part1.GND, LCD.pin1, Power_Sensor.pin4
  LOAD 3: U1.D5, Module_Relay.pin4
  RX ESP: U1.RX, Part1.LV1
  TX ESP: U1.TX, Part1.LV2
  5V: U1.Vin, Module_Relay.pin1, Part1.HV, LCD.pin2, Power_Sensor.pin1
  Buzzer: Buzzer.pin2
  TX: Part1.HV1, Power_Sensor.pin3
  RX: Part1.HV2, Power_Sensor.pin2
  SDA: Part1.HV3, LCD.pin3
  SCL: Part1.HV4, LCD.pin4

notes:
  Power Metter, ĐỒ ÁN MÔN HỌC                                                   CẢM BIẾN TRONG ĐO LƯỜNG, 1.0.0

custom parts:
  NodeMCU V1.0: ESP8266 based NodeMCU
